# Fritzing sketch SmartMote_v1 (saved by Fritzing 0.9.3b)
circuit board: 8.46667cm x 5.64444cm
breadboards: 1

parts:
  Photon = Photon
  Part1 = Adafruit Latching Mini Relay FeatherWing [part_number="Adafruit #2923"]
  Part2 = NeoPixel Stick [part_number=1426]

nets:
  GND: Photon.GND, Part1.GND, Part2.GND
  VIN: Photon.VIN, Part2.+5V
  N1: Photon.D2, Part2.DATAIN
  N2: Photon.D3, Part1.SET
  N3: Photon.D4, Part1.UNSET
  N4: Photon.3V3, Part1.AREF

custom parts:
  Adafruit Latching Mini Relay FeatherWing: A Feather board without ambition is a Feather board without FeatherWings! This is the Latching Mini Relay FeatherWing. It gives you power to control, and control over power. Put simply, you can now turn on and off lamps, fans, solenoids, and other small appliances that run on up to 250VAC or DC power using any Feather board. The are two 'flavors' of these FeatherWings, this is the Latching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
  NeoPixel Stick: Make your own little LED strip arrangement with this stick of NeoPixel LEDs. We crammed 8 of the tiny 5050 (5mm x 5mm) smart RGB LEDs onto a PCB with mounting holes and a chainable design. Use only one microcontroller pin to control as many as you can chain together! Each LED is addressable as the driver chip is inside the LED. Each one has ~18mA constant current drive so the color will be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
